# Fritzing sketch confort (saved by Fritzing 0.9.3b)
breadboards: 1

parts:
  Composant1 = Arduino Uno (Rev3)
  Grove1 = Grove 3 Axis Digital Accelerometer 16g
  KY-2 = Keyes Relay [package=THT]
  VCC1 = Battery block 9V
  L2 = bulb_holder_E10_with_base

nets:
  N1: Composant1.A4/SDA, Grove1.SDA
  N2: Composant1.A5/SCL, Grove1.SCL
  N3: Composant1.D3_PWM, KY-2.ground
  3V3: Composant1.3V3, Grove1.VCC
  GND: Composant1.GND, Grove1.GND, KY-2.power
  N4: KY-2.C, VCC1.-
  N5: KY-2.NO, L2.connector0
  N6: VCC1.+, L2.connector1

custom parts:
  Keyes Relay: The Keyes 5V relay module is suitable for SCM development, home appliance control. It uses a 5V~12V TIL control signal which can control DC / AC signal.
