# Fritzing sketch regroupement (saved by Fritzing 0.9.3b)

parts:
  Composant1 = Adafruit TSL2561 [part_number="Adafruit #439"]
  Composant2 = Arduino Uno (Rev3)

nets:
  VIN: Composant1.VIN, Composant2.3V3
  GND: Composant1.GND, Composant2.GND
  N1: Composant1.INT, Composant1.SDA, Composant2.A5/SCL
  N2: Composant1.SCL, Composant2.A4/SDA

custom parts:
  Adafruit TSL2561: The TSL2561 luminosity sensor is an advanced digital light sensor, ideal for use in a wide range of light situations. Compared to low cost CdS cells, this sensor is more precise, allowing for exact lux calculations and can be configured for different gain/timing ranges to detect light ranges from up to 0.1 - 40,000+ Lux on the fly. The best part of this sensor is that it contains both infrared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
