# Fritzing sketch RTC_SSD_CE (saved by Fritzing 0.9.3b)
breadboards: 1

parts:
  Composant1 = Arduino Uno (Rev3)
  Composant2 = MicroSD Card Module
  Composant3 = Real Time Clock Module - DS1307 RTC Breakout Board

nets:
  N1: Composant1.D10_PWM/SS, Composant2.GND
  N2: Composant1.D11_PWM/MOSI, Composant2.MISO
  N3: Composant1.D12/MISO, Composant2.MOSI
  N4: Composant1.D13/SCK, Composant2.VCC
  N5: Composant1.A4/SDA, Composant3.SDA
  N6: Composant1.A5/SCL, Composant3.SCL
  5V: Composant1.5V, Composant2.SCK, Composant3.5V
  GND: Composant1.GND, Composant3.GND
