# Fritzing sketch Montage_ArduinoMega_Bluetooth (saved by Fritzing 0.9.3b)
breadboards: 1

parts:
  Composant1 = Arduino Mega 2560 (Rev3)
  Composant2 = Bluetooth HC-05 Macho

nets:
  N1: Composant1.D19/RX1, Composant2.TXD
  N2: Composant1.D18/TX1, Composant2.RXD
  GND: Composant1.GND, Composant2.GND
  5V: Composant1.5V, Composant2.VCC
